// Logisim project riscv.circ as structural Verilog: 8 circuits, main circuit main
module main (
  input  in_1,
  output [31:0] out_2,
  output [31:0] out_3,
  output [31:0] out_4,
  output [31:0] out_5,
  output [31:0] out_6,
  output [31:0] out_7,
  output [4:0] out_8
);

  wire alu_1_aluzero, and_1_out, button_1_out, clock_1_out, controlunit_1_alusrc, controlunit_1_branch,
       controlunit_1_jump, controlunit_1_memread, controlunit_1_memtoreg, controlunit_1_memwrite,
       controlunit_1_regwrite, or_1_out, xor_1_out;
  wire [1:0] controlunit_1_aluops;
  wire [3:0] alucontrolunit_1_alucu_out;
  wire [31:0] multiplexer_1_out, ram_1_dout, regfile_1_readregout1, regfile_1_readregout2, shifter_1_out;

  Clock clock_1 (.out(clock_1_out));
  Button button_1 (.out(button_1_out));
  Adder #(.width(32)) adder_1 (.a(out_3), .b(out_6), .out(out_2), .cin(1'b0));  // open: cout
  PC pc_1 (
    .address_to_load(out_2), .CLK(clock_1_out), .load_address(or_1_out), .PC_enable(in_1),
    .areset(button_1_out), .Output_PC(out_3));
  Shifter #(.shift("lr"), .width(32)) shifter_1 (.in(out_3), .\dist (5'b00010), .out(shifter_1_out));
  ROM #(.dataWidth(32)) rom_1 (.addr(shifter_1_out[7:0]), .data(out_4));
  or or_1 (or_1_out, and_1_out, controlunit_1_jump);
  and and_1 (and_1_out, xor_1_out, controlunit_1_branch);
  ControlUnit controlunit_1 (
    .instruction(out_4), .MemWrite(controlunit_1_memwrite), .ALUOps(controlunit_1_aluops),
    .RegWrite(controlunit_1_regwrite), .ALUSrc(controlunit_1_alusrc), .MemRead(controlunit_1_memread),
    .Branch(controlunit_1_branch), .MemtoReg(controlunit_1_memtoreg), .Jump(controlunit_1_jump));
  xor xor_1 (xor_1_out, alu_1_aluzero, out_4[12]);
  ImmGen immgen_1 (
    .Branch(controlunit_1_branch), .Jump(controlunit_1_jump), .MemWrite(controlunit_1_memwrite),
    .instruction_in(out_4), .imm_out(out_6));
  ALUControlUnit alucontrolunit_1 (
    .ALUOp(controlunit_1_aluops), .funct3(out_4[14:12]), .funct7(out_4[30]),
    .ALUCU_OUT(alucontrolunit_1_alucu_out));
  RegFile regfile_1 (
    .ReadReg1Addr(out_4[19:15]), .ReadReg2Addr(out_4[24:20]), .WriteRegAddr(out_4[11:7]),
    .areset(button_1_out), .CLK(clock_1_out), .DATA(out_7), .RegWriteEna(controlunit_1_regwrite),
    .ReadRegOut1(regfile_1_readregout1), .ReadRegOut2(regfile_1_readregout2));
  Multiplexer #(.width(32)) multiplexer_1 (
    .in0(regfile_1_readregout2), .in1(out_6), .out(multiplexer_1_out), .sel(controlunit_1_alusrc));
  ALU alu_1 (
    .ALUOps_in(alucontrolunit_1_alucu_out), .x(regfile_1_readregout1), .y(multiplexer_1_out),
    .ALUZero(alu_1_aluzero), .ALUOut(out_5));
  RAM #(.dataWidth(32)) ram_1 (
    .addr(out_5[7:0]), .we(controlunit_1_memwrite), .oe(controlunit_1_memread), .clk(clock_1_out),
    .din(regfile_1_readregout2), .dout(ram_1_dout));
  Multiplexer #(.width(32)) multiplexer_2 (.in0(out_5), .in1(ram_1_dout), .out(out_7), .sel(controlunit_1_memtoreg));

  assign out_8 = out_4[11:7];

  // Notes on the sheet:
  //   contents of rom_1 (hex, n*v repeats v):
  //   93 a00113 2080b3 fff10113 fe011ce3 193 11a023 12283 100006f 13 13 13 528293
  //   MemtoRegMux
endmodule

module PC (
  input  [31:0] address_to_load,
  input  CLK,
  input  load_address,
  input  PC_enable,
  input  areset,
  output [31:0] Output_PC
);

  wire adder_1_cout;
  wire [31:0] adder_1_out, multiplexer_1_out;

  Register #(.width(32)) register_1 (.D(multiplexer_1_out), .en(PC_enable), .clk(CLK), .Q(Output_PC), .clr(areset));
  Multiplexer #(.width(32)) multiplexer_1 (
    .in0(adder_1_out), .in1(address_to_load), .out(multiplexer_1_out), .sel(load_address));
  Adder #(.width(32)) adder_1 (.a(32'h4), .b(Output_PC), .out(adder_1_out), .cin(1'b0), .cout(adder_1_cout));
  // also tied to GND on the sheet: adder_1_cout
endmodule

module RegFile (
  input  [4:0] ReadReg1Addr,
  input  [4:0] ReadReg2Addr,
  input  [4:0] WriteRegAddr,
  input  areset,
  input  CLK,
  input  [31:0] DATA,
  input  RegWriteEna,
  output [31:0] ReadRegOut1,
  output [31:0] ReadRegOut2
);

  wire x0_ena, x1_ena, x2_ena, x3_ena, x4_ena, x5_ena, x6_ena, x7_ena, x8_ena, x9_ena, x10_ena, x11_ena,
       x12_ena, x13_ena, x14_ena, x15_ena, x16_ena, x17_ena, x18_ena, x19_ena, x20_ena, x21_ena, x22_ena,
       x23_ena, x24_ena, x25_ena, x26_ena, x27_ena, x28_ena, x29_ena, x30_ena, x31_ena;
  wire [31:0] x1_data, x2_data, x3_data, x4_data, x5_data, x6_data, x7_data, x8_data, x9_data, x10_data,
       x11_data, x12_data, x13_data, x14_data, x15_data, x16_data, x17_data, x18_data, x19_data, x20_data,
       x21_data, x22_data, x23_data, x24_data, x25_data, x26_data, x27_data, x28_data, x29_data, x30_data,
       x31_data;

  Decoder #(.enable("false"), .select(5)) decoder_1 (
    .out0(x0_ena), .out1(x1_ena), .out2(x2_ena), .out3(x3_ena), .out4(x4_ena), .out5(x5_ena), .out6(x6_ena),
    .out7(x7_ena), .out8(x8_ena), .out9(x9_ena), .out10(x10_ena), .out11(x11_ena), .out12(x12_ena),
    .out13(x13_ena), .out14(x14_ena), .out15(x15_ena), .out16(x16_ena), .out17(x17_ena), .out18(x18_ena),
    .out19(x19_ena), .out20(x20_ena), .out21(x21_ena), .out22(x22_ena), .out23(x23_ena), .out24(x24_ena),
    .out25(x25_ena), .out26(x26_ena), .out27(x27_ena), .out28(x28_ena), .out29(x29_ena), .out30(x30_ena),
    .out31(x31_ena), .sel(WriteRegAddr));
  WriteSignalReg writesignalreg_1 (
    .write_ena(x4_ena), .write_sig(RegWriteEna), .CLK(CLK), .DATA(DATA), .areset(areset), .data_out(x4_data));
  WriteSignalReg writesignalreg_2 (
    .write_ena(x8_ena), .write_sig(RegWriteEna), .CLK(CLK), .DATA(DATA), .areset(areset), .data_out(x8_data));
  WriteSignalReg writesignalreg_3 (
    .write_ena(x12_ena), .write_sig(RegWriteEna), .CLK(CLK), .DATA(DATA), .areset(areset), .data_out(x12_data));
  WriteSignalReg writesignalreg_4 (
    .write_ena(x16_ena), .write_sig(RegWriteEna), .CLK(CLK), .DATA(DATA), .areset(areset), .data_out(x16_data));
  WriteSignalReg writesignalreg_5 (
    .write_ena(x20_ena), .write_sig(RegWriteEna), .CLK(CLK), .DATA(DATA), .areset(areset), .data_out(x20_data));
  WriteSignalReg writesignalreg_6 (
    .write_ena(x24_ena), .write_sig(RegWriteEna), .CLK(CLK), .DATA(DATA), .areset(areset), .data_out(x24_data));
  WriteSignalReg writesignalreg_7 (
    .write_ena(x28_ena), .write_sig(RegWriteEna), .CLK(CLK), .DATA(DATA), .areset(areset), .data_out(x28_data));
  WriteSignalReg writesignalreg_8 (
    .write_ena(x1_ena), .write_sig(RegWriteEna), .CLK(CLK), .DATA(DATA), .areset(areset), .data_out(x1_data));
  WriteSignalReg writesignalreg_9 (
    .write_ena(x5_ena), .write_sig(RegWriteEna), .CLK(CLK), .DATA(DATA), .areset(areset), .data_out(x5_data));
  WriteSignalReg writesignalreg_10 (
    .write_ena(x9_ena), .write_sig(RegWriteEna), .CLK(CLK), .DATA(DATA), .areset(areset), .data_out(x9_data));
  WriteSignalReg writesignalreg_11 (
    .write_ena(x13_ena), .write_sig(RegWriteEna), .CLK(CLK), .DATA(DATA), .areset(areset), .data_out(x13_data));
  WriteSignalReg writesignalreg_12 (
    .write_ena(x17_ena), .write_sig(RegWriteEna), .CLK(CLK), .DATA(DATA), .areset(areset), .data_out(x17_data));
  WriteSignalReg writesignalreg_13 (
    .write_ena(x21_ena), .write_sig(RegWriteEna), .CLK(CLK), .DATA(DATA), .areset(areset), .data_out(x21_data));
  WriteSignalReg writesignalreg_14 (
    .write_ena(x25_ena), .write_sig(RegWriteEna), .CLK(CLK), .DATA(DATA), .areset(areset), .data_out(x25_data));
  WriteSignalReg writesignalreg_15 (
    .write_ena(x29_ena), .write_sig(RegWriteEna), .CLK(CLK), .DATA(DATA), .areset(areset), .data_out(x29_data));
  WriteSignalReg writesignalreg_16 (
    .write_ena(x2_ena), .write_sig(RegWriteEna), .CLK(CLK), .DATA(DATA), .areset(areset), .data_out(x2_data));
  WriteSignalReg writesignalreg_17 (
    .write_ena(x6_ena), .write_sig(RegWriteEna), .CLK(CLK), .DATA(DATA), .areset(areset), .data_out(x6_data));
  WriteSignalReg writesignalreg_18 (
    .write_ena(x10_ena), .write_sig(RegWriteEna), .CLK(CLK), .DATA(DATA), .areset(areset), .data_out(x10_data));
  WriteSignalReg writesignalreg_19 (
    .write_ena(x14_ena), .write_sig(RegWriteEna), .CLK(CLK), .DATA(DATA), .areset(areset), .data_out(x14_data));
  WriteSignalReg writesignalreg_20 (
    .write_ena(x18_ena), .write_sig(RegWriteEna), .CLK(CLK), .DATA(DATA), .areset(areset), .data_out(x18_data));
  WriteSignalReg writesignalreg_21 (
    .write_ena(x22_ena), .write_sig(RegWriteEna), .CLK(CLK), .DATA(DATA), .areset(areset), .data_out(x22_data));
  WriteSignalReg writesignalreg_22 (
    .write_ena(x26_ena), .write_sig(RegWriteEna), .CLK(CLK), .DATA(DATA), .areset(areset), .data_out(x26_data));
  WriteSignalReg writesignalreg_23 (
    .write_ena(x30_ena), .write_sig(RegWriteEna), .CLK(CLK), .DATA(DATA), .areset(areset), .data_out(x30_data));
  WriteSignalReg writesignalreg_24 (
    .write_ena(x3_ena), .write_sig(RegWriteEna), .CLK(CLK), .DATA(DATA), .areset(areset), .data_out(x3_data));
  WriteSignalReg writesignalreg_25 (
    .write_ena(x7_ena), .write_sig(RegWriteEna), .CLK(CLK), .DATA(DATA), .areset(areset), .data_out(x7_data));
  WriteSignalReg writesignalreg_26 (
    .write_ena(x11_ena), .write_sig(RegWriteEna), .CLK(CLK), .DATA(DATA), .areset(areset), .data_out(x11_data));
  WriteSignalReg writesignalreg_27 (
    .write_ena(x15_ena), .write_sig(RegWriteEna), .CLK(CLK), .DATA(DATA), .areset(areset), .data_out(x15_data));
  WriteSignalReg writesignalreg_28 (
    .write_ena(x19_ena), .write_sig(RegWriteEna), .CLK(CLK), .DATA(DATA), .areset(areset), .data_out(x19_data));
  WriteSignalReg writesignalreg_29 (
    .write_ena(x23_ena), .write_sig(RegWriteEna), .CLK(CLK), .DATA(DATA), .areset(areset), .data_out(x23_data));
  WriteSignalReg writesignalreg_30 (
    .write_ena(x27_ena), .write_sig(RegWriteEna), .CLK(CLK), .DATA(DATA), .areset(areset), .data_out(x27_data));
  WriteSignalReg writesignalreg_31 (
    .write_ena(x31_ena), .write_sig(RegWriteEna), .CLK(CLK), .DATA(DATA), .areset(areset), .data_out(x31_data));
  Multiplexer #(.select(5), .width(32)) multiplexer_1 (
    .in0({32{1'b0}}), .in1(x1_data), .in2(x2_data), .in3(x3_data), .in4(x4_data), .in5(x5_data),
    .in6(x6_data), .in7(x7_data), .in8(x8_data), .in9(x9_data), .in10(x10_data), .in11(x11_data),
    .in12(x12_data), .in13(x13_data), .in14(x14_data), .in15(x15_data), .in16(x16_data), .in17(x17_data),
    .in18(x18_data), .in19(x19_data), .in20(x20_data), .in21(x21_data), .in22(x22_data), .in23(x23_data),
    .in24(x24_data), .in25(x25_data), .in26(x26_data), .in27(x27_data), .in28(x28_data), .in29(x29_data),
    .in30(x30_data), .in31(x31_data), .out(ReadRegOut1), .sel(ReadReg1Addr));
  Multiplexer #(.select(5), .width(32)) multiplexer_2 (
    .in0({32{1'b0}}), .in1(x1_data), .in2(x2_data), .in3(x3_data), .in4(x4_data), .in5(x5_data),
    .in6(x6_data), .in7(x7_data), .in8(x8_data), .in9(x9_data), .in10(x10_data), .in11(x11_data),
    .in12(x12_data), .in13(x13_data), .in14(x14_data), .in15(x15_data), .in16(x16_data), .in17(x17_data),
    .in18(x18_data), .in19(x19_data), .in20(x20_data), .in21(x21_data), .in22(x22_data), .in23(x23_data),
    .in24(x24_data), .in25(x25_data), .in26(x26_data), .in27(x27_data), .in28(x28_data), .in29(x29_data),
    .in30(x30_data), .in31(x31_data), .out(ReadRegOut2), .sel(ReadReg2Addr));

  // Other names for the same wires on the sheet: DATA_IN[31:0] = DATA; MUXRegRead1[31:0] = ReadRegOut1;
  //   MUXRegRead2[31:0] = ReadRegOut2; REG1_ADDR[4:0] = ReadReg1Addr; REG2_ADDR[4:0] = ReadReg2Addr;
  //   WRITE_ADDR[4:0] = WriteRegAddr; WRITE_SIG = RegWriteEna
endmodule

module WriteSignalReg (
  input  [31:0] DATA,
  input  write_ena,
  input  write_sig,
  input  CLK,
  input  areset,
  output [31:0] data_out
);

  wire and_1_out;

  and and_1 (and_1_out, write_ena, write_sig);
  Register #(.width(32)) register_1 (.D(DATA), .en(and_1_out), .clk(CLK), .Q(data_out), .clr(areset));
endmodule

module ControlUnit (
  input  [31:0] instruction,
  output MemWrite,
  output [1:0] ALUOps,
  output RegWrite,
  output ALUSrc,
  output MemRead,
  output Branch,
  output MemtoReg,
  output Jump
);

  wire ITYPE, or_2_out, RTYPE;

  Comparator #(.width(7)) comparator_1 (.a(instruction[6:0]), .b(7'b0110011), .eq(RTYPE));  // open: gt, lt
  Comparator #(.width(7)) comparator_2 (.a(instruction[6:0]), .b(7'b0010011), .eq(ITYPE));  // open: gt, lt
  Comparator #(.width(7)) comparator_3 (.a(instruction[6:0]), .b(7'b0100011), .eq(MemWrite));  // open: gt, lt
  Comparator #(.width(7)) comparator_4 (.a(instruction[6:0]), .b(7'b1100011), .eq(Branch));  // open: gt, lt
  Comparator #(.width(7)) comparator_5 (.a(instruction[6:0]), .b(7'b1101111), .eq(Jump));  // open: gt, lt
  Comparator #(.width(7)) comparator_6 (.a(instruction[6:0]), .b(7'b0000011), .eq(MemRead));  // open: gt, lt
  or or_1 (RegWrite, RTYPE, ITYPE, MemRead, Jump);
  or or_2 (or_2_out, MemRead, ITYPE, Jump, MemWrite);
  Priority_Encoder #(.select(2)) priority_encoder_1 (
    .in0(or_2_out), .in1(Branch), .in2(RTYPE), .out(ALUOps), .en_in(1'b1));  // open: in3, gs, en_out
  or or_3 (ALUSrc, MemWrite, ITYPE, MemRead, Jump);

  assign MemtoReg = MemRead;

  // Other names for the same wires on the sheet: BTYPE = Branch; OP_CODE[6:0] = instruction[6:0];
  //   rd[4:0] = instruction[11:7]; funct3[2:0] = instruction[14:12]; rs1[4:0] = instruction[19:15];
  //   rs2[4:0] = instruction[24:20]; funct7[6:0] = instruction[31:25]; JTYPE = Jump; LOAD_TYPE = MemRead;
  //   STYPE = MemWrite

  // Notes on the sheet:
  //   R-TYPE
  //   I-TYPE Load
endmodule

module ALU (
  input  [31:0] x,
  input  [31:0] y,
  input  [3:0] ALUOps_in,
  output ALUZero,
  output [31:0] ALUOut
);

  wire adder_1_cout, subtractor_1_bout;
  wire [31:0] ALU_Add, ALU_And, ALU_OR, ALU_Sub, ALU_XOR;

  Adder #(.width(32)) adder_1 (.a(x), .b(y), .out(ALU_Add), .cin(1'b0), .cout(adder_1_cout));
  Subtractor #(.width(32)) subtractor_1 (.a(x), .b(y), .out(ALU_Sub), .bout(subtractor_1_bout));  // open: bin
  assign ALU_And = x & y;  // AND_Gate and_1, 32 bits wide
  assign ALU_OR = x | y;  // OR_Gate or_1, 32 bits wide
  assign ALU_XOR = x ^ y;  // XOR_Gate xor_1, 32 bits wide
  Comparator #(.width(32)) comparator_1 (.a(ALUOut), .b({32{1'b0}}), .eq(ALUZero));  // open: gt, lt
  Multiplexer #(.select(4), .width(32)) multiplexer_1 (
    .in0(ALU_And), .in1(ALU_OR), .in2(ALU_Add), .in3(ALU_XOR), .in6(ALU_Sub), .out(ALUOut), .sel(ALUOps_in));  // open: in4, in5, in7, in8, in9, in10, in11, in12, in13, in14, in15

  // Other names for the same wires on the sheet: MUX_OUT[31:0] = ALUOut; x_tun[31:0] = x; y_tun[31:0] = y
endmodule

module ALUControlUnit (
  input  [1:0] ALUOp,
  input  [2:0] funct3,
  input  funct7,
  output [3:0] ALUCU_OUT
);

  wire and_1_out, not_1_out, not_2_out, not_3_out, not_4_out;

  not not_1 (not_1_out, ALUOp[1]);
  not not_2 (not_2_out, funct3[2]);
  not not_3 (not_3_out, funct3[1]);
  not not_4 (not_4_out, funct3[0]);
  and and_1 (and_1_out, ALUOp[1], not_2_out, funct7);
  or or_1 (ALUCU_OUT[1], not_1_out, not_3_out);
  and and_2 (ALUCU_OUT[0], ALUOp[1], funct3[2], not_4_out);
  or or_2 (ALUCU_OUT[2], ALUOp[0], and_1_out);

  assign ALUCU_OUT[3] = 1'b0;
endmodule

module ImmGen (
  input  Branch,
  input  Jump,
  input  MemWrite,
  input  [31:0] instruction_in,
  output [31:0] imm_out
);

  wire ImmSel1, ImmSel2;
  wire [31:0] BTYPE_IMM, ITYPE_IMM, JTYPE_IMM, STYPE_IMM;

  assign BTYPE_IMM = {{19{instruction_in[31]}}, {instruction_in[31], instruction_in[7], instruction_in[30:25], instruction_in[11:8], 1'b0}};  // Bit_Extender bit_extender_1
  assign JTYPE_IMM = {{11{instruction_in[31]}}, {instruction_in[31], instruction_in[19:12], instruction_in[20], instruction_in[30:21], 1'b0}};  // Bit_Extender bit_extender_2
  assign STYPE_IMM = {{20{instruction_in[31]}}, {instruction_in[31:25], instruction_in[11:7]}};  // Bit_Extender bit_extender_3
  assign ITYPE_IMM = {{20{instruction_in[31]}}, instruction_in[31:20]};  // Bit_Extender bit_extender_4
  or or_1 (ImmSel1, Branch, Jump);
  or or_2 (ImmSel2, Jump, MemWrite);
  Multiplexer #(.select(2), .width(32)) multiplexer_1 (
    .in0(ITYPE_IMM), .in1(STYPE_IMM), .in2(BTYPE_IMM), .in3(JTYPE_IMM), .out(imm_out),
    .sel({ImmSel1, ImmSel2}));

  // Notes on the sheet:
  //   I-type, set branch, write, jump to 0
  //   B-type, set branch to 1
  //   S-type, set memwrite to 1
  //   J-type, set jump to 1
  //   Positive test
  //   00500093 -> 00000005
  //   00802103 -> 00000008
  //   00202623 -> 0000000C
  //   00000863 -> 00000010
  //   020000EF -> 00000020
  //   Negative Tests
  //   FFF00093 -> FFFFFFFF
  //   FFC02103 -> FFFFFFFC
  //   FE202C23 -> FFFFFFF8
  //   FE000CE3 -> FFFFFFF8
  //   FE1FF0EF -> FFFFFFE0
endmodule
